# Fritzing sketch solar tracker (saved by Fritzing 0.9.3b)
breadboards: 1

parts:
  Part1 = Arduino Nano (Rev3.0)
  BAT1 = Battery Holders [package=lipo-1100mAh]
  BAT2 = Battery Holders [package=lipo-1100mAh]  # not connected
  BAT3 = Battery Holders [package=lipo-1100mAh]
  R1 = Photocell (LDR) [package=THT]
  R2 = Photocell (LDR) [package=THT]
  R3 = Photocell (LDR) [package=THT]
  R4 = Photocell (LDR) [package=THT]
  J1 = Basic Servo
  J2 = Basic Servo
  D1 = Diode [package=diode-1n4148]
  R5 = Resistor [tolerance=±5% resistance=220 package="2010 [SMD]"]
  R6 = Resistor [tolerance=±5% resistance=220 package="2010 [SMD]"]
  R7 = Resistor [tolerance=±5% resistance=220 package="2010 [SMD]"]
  R8 = Resistor [tolerance=±5% resistance=220 package="2010 [SMD]"]
  D2 = SOLAR-IXYS [package=solarbit-12x1]
  IC1 = Voltage Regulator [package=to-220-alt]
  S1 = SWITCH-MOMENTARY-2 [package=tactile-switch-1101ne]

nets:
  GND: Part1.GND, BAT3.-, R1.pin_0, R2.pin_0, R3.pin_0, R4.pin_0, J1.gnd, J2.gnd, D2.A, IC1.GND
  VCC: Part1.VIN, J1.vcc, J2.vcc, R5.Pin_1, R6.Pin_1, R7.Pin_1, R8.Pin_1, IC1.OUT
  N1: Part1.A7, J1.pulse
  N2: Part1.A6, J2.pulse
  N3: Part1.A4, R4.pin_1, R8.Pin_0
  N4: Part1.A3, R3.pin_1, R7.Pin_0
  N5: Part1.A2, R2.pin_1, R6.Pin_0
  N6: Part1.A1, R1.pin_1, R5.Pin_0
  N7: BAT1.+, D2.C, S1.2
  N8: D1.A, S1.1
  N9: D1.C, IC1.IN
